// Logisim project machine.circ as structural Verilog: 24 circuits, main circuit main
module main (
  input  [31:0] A,
  input  [31:0] B,
  input  [5:0] in_3,
  output [31:0] OUTPUT,
  output N,
  output Z
);

  // Probe on A
  // Probe on B
  _32bit_ALU u_32bit_alu_1 (
    .A(A), .B(B), .out_10(OUTPUT), .F1(in_3[4]), .F0(in_3[5]), .ENB(in_3[2]), .ENA(in_3[3]), .INVA(in_3[1]),
    .in_8(in_3[0]), .Zero_Flag(Z), .Negative_Flag(N));
  // Probe on OUTPUT

  // Notes on the sheet:
  //   32-Bit ALU and Shifter
  //   Alex Nardozzi
  //   Tyler Griffith
  //   Yonatan Belayhun
endmodule

module _1_bit_full_adder (
  input  in_1,
  input  in_2,
  input  in_3,
  input  in_4,
  output out_5,
  output out_6
);

  wire and_1_out, and_2_out, xor_1_out, xor_2_out;

  and and_1 (and_1_out, in_2, in_4, in_3);
  xor xor_1 (xor_1_out, in_2, in_3);
  or or_1 (out_6, and_1_out, and_2_out);
  and and_2 (and_2_out, in_1, in_4, xor_1_out);
  xor xor_2 (xor_2_out, in_1, xor_1_out);
  and and_3 (out_5, xor_2_out, in_4);
endmodule

module _1_bit_ALU (
  input  Carry_in,
  input  INVA,
  input  A,
  input  ENA,
  input  B,
  input  ENB,
  input  F0,
  input  F1,
  output Output,
  output Carry_Out
);

  wire and_1_out, and_2_out, and_3_out, and_4_out, and_5_out, and_6_out, decoder_1_out_3, decoder_1_out_4,
       decoder_1_out_5, decoder_1_out_6, n1_bit_full_adder_1_out_5, not_1_out, or_1_out, xor_1_out;

  and and_1 (and_1_out, A, ENA);
  and and_2 (and_2_out, B, ENB);
  Decoder decoder_1 (
    .in_1(F0), .in_2(F1), .out_3(decoder_1_out_3), .out_4(decoder_1_out_4), .out_5(decoder_1_out_5),
    .out_6(decoder_1_out_6));
  xor xor_1 (xor_1_out, INVA, and_1_out);
  and and_3 (and_3_out, xor_1_out, and_2_out);
  or or_1 (or_1_out, xor_1_out, and_2_out);
  not not_1 (not_1_out, and_2_out);
  and and_4 (and_4_out, and_3_out, decoder_1_out_3);
  and and_5 (and_5_out, or_1_out, decoder_1_out_4);
  and and_6 (and_6_out, not_1_out, decoder_1_out_5);
  _1_bit_full_adder u_1_bit_full_adder_1 (
    .in_2(and_2_out), .in_3(xor_1_out), .in_4(decoder_1_out_6), .in_1(Carry_in), .out_6(Carry_Out),
    .out_5(n1_bit_full_adder_1_out_5));
  or or_2 (Output, and_4_out, and_5_out, and_6_out, n1_bit_full_adder_1_out_5);
endmodule

module Decoder (
  input  in_1,
  input  in_2,
  output out_3,
  output out_4,
  output out_5,
  output out_6
);

  wire not_1_out, not_2_out, not_3_out, not_4_out;

  not not_1 (not_1_out, in_1);
  not not_2 (not_2_out, in_2);
  not not_3 (not_3_out, in_1);
  not not_4 (not_4_out, in_2);
  and and_1 (out_3, not_1_out, not_2_out);
  and and_2 (out_4, not_3_out, in_2);
  and and_3 (out_5, in_1, not_4_out);
  and and_4 (out_6, in_1, in_2);
endmodule

module _8_bit_ALU (
  input  in_1,
  input  F1,
  input  F0,
  input  ENB,
  input  ENA,
  input  INVA,
  input  [7:0] A,
  input  [7:0] B,
  output [7:0] out_9,
  output out_10
);

  wire n1_bit_alu_1_carry_out, n1_bit_alu_2_carry_out, n1_bit_alu_3_carry_out, n1_bit_alu_4_carry_out,
       n1_bit_alu_5_carry_out, n1_bit_alu_6_carry_out, n1_bit_alu_7_carry_out;

  _1_bit_ALU u_1_bit_alu_1 (
    .INVA(INVA), .A(A[0]), .ENA(ENA), .B(B[0]), .ENB(ENB), .F0(F0), .F1(F1), .Output(out_9[0]),
    .Carry_in(in_1), .Carry_Out(n1_bit_alu_1_carry_out));
  _1_bit_ALU u_1_bit_alu_2 (
    .INVA(INVA), .A(A[1]), .ENA(ENA), .B(B[1]), .ENB(ENB), .F0(F0), .F1(F1), .Output(out_9[1]),
    .Carry_in(n1_bit_alu_1_carry_out), .Carry_Out(n1_bit_alu_2_carry_out));
  _1_bit_ALU u_1_bit_alu_3 (
    .INVA(INVA), .A(A[2]), .ENA(ENA), .B(B[2]), .ENB(ENB), .F0(F0), .F1(F1), .Output(out_9[2]),
    .Carry_in(n1_bit_alu_2_carry_out), .Carry_Out(n1_bit_alu_3_carry_out));
  _1_bit_ALU u_1_bit_alu_4 (
    .INVA(INVA), .A(A[3]), .ENA(ENA), .B(B[3]), .ENB(ENB), .F0(F0), .F1(F1), .Output(out_9[3]),
    .Carry_in(n1_bit_alu_3_carry_out), .Carry_Out(n1_bit_alu_4_carry_out));
  _1_bit_ALU u_1_bit_alu_5 (
    .INVA(INVA), .A(A[4]), .ENA(ENA), .B(B[4]), .ENB(ENB), .F0(F0), .F1(F1), .Output(out_9[4]),
    .Carry_in(n1_bit_alu_4_carry_out), .Carry_Out(n1_bit_alu_5_carry_out));
  _1_bit_ALU u_1_bit_alu_6 (
    .INVA(INVA), .A(A[5]), .ENA(ENA), .B(B[6]), .ENB(ENB), .F0(F0), .F1(F1), .Output(out_9[5]),
    .Carry_in(n1_bit_alu_5_carry_out), .Carry_Out(n1_bit_alu_6_carry_out));
  _1_bit_ALU u_1_bit_alu_7 (
    .INVA(INVA), .A(A[6]), .ENA(ENA), .B(B[5]), .ENB(ENB), .F0(F0), .F1(F1), .Output(out_9[6]),
    .Carry_in(n1_bit_alu_6_carry_out), .Carry_Out(n1_bit_alu_7_carry_out));
  _1_bit_ALU u_1_bit_alu_8 (
    .INVA(INVA), .A(A[7]), .ENA(ENA), .B(B[7]), .ENB(ENB), .F0(F0), .F1(F1), .Output(out_9[7]),
    .Carry_in(n1_bit_alu_7_carry_out), .Carry_Out(out_10));
endmodule

module _32bit_ALU (
  input  [31:0] A,
  input  [31:0] B,
  input  F1,
  input  F0,
  input  ENB,
  input  ENA,
  input  INVA,
  input  in_8,
  output Zero_Flag,
  output [31:0] out_10,
  output Negative_Flag
);

  wire n8_bit_alu_1_out_10, n8_bit_alu_2_out_10, n8_bit_alu_3_out_10;

  _8_bit_ALU u_8_bit_alu_1 (
    .A(A[7:0]), .B(B[7:0]), .out_9(out_10[7:0]), .F1(F1), .F0(F0), .ENB(ENB), .ENA(ENA), .INVA(INVA),
    .in_1(in_8), .out_10(n8_bit_alu_1_out_10));
  _8_bit_ALU u_8_bit_alu_2 (
    .A(A[15:8]), .B(B[15:8]), .out_9(out_10[15:8]), .F1(F1), .F0(F0), .ENB(ENB), .ENA(ENA), .INVA(INVA),
    .in_1(n8_bit_alu_1_out_10), .out_10(n8_bit_alu_2_out_10));
  _8_bit_ALU u_8_bit_alu_3 (
    .A(A[23:16]), .B(B[23:16]), .out_9(out_10[23:16]), .F1(F1), .F0(F0), .ENB(ENB), .ENA(ENA), .INVA(INVA),
    .in_1(n8_bit_alu_2_out_10), .out_10(n8_bit_alu_3_out_10));
  _8_bit_ALU u_8_bit_alu_4 (
    .A(A[31:24]), .B(B[31:24]), .out_9({Negative_Flag, out_10[30:24]}), .F1(F1), .F0(F0), .ENB(ENB),
    .ENA(ENA), .INVA(INVA), .in_1(n8_bit_alu_3_out_10));  // open: out_10
  nor nor_1 (Zero_Flag, out_10[7], out_10[6], out_10[5], out_10[4], out_10[3], out_10[2], out_10[1], out_10[0], out_10[15], out_10[14], out_10[13], out_10[12], out_10[11], out_10[10], out_10[9], out_10[8], out_10[23], out_10[22], out_10[21], out_10[20], out_10[19], out_10[18], out_10[17], out_10[16], Negative_Flag, out_10[30], out_10[29], out_10[28], out_10[27], out_10[26], out_10[25], out_10[24]);

  assign out_10[31] = Negative_Flag;
endmodule

module Shifter (
  input  [31:0] in_1,
  input  [1:0] in_2,
  output [31:0] OUTPUT
);

  wire and_1_out, and_2_out, and_3_out, not_1_out, not_2_out;
  wire [4:0] bit_extender_1_out;
  wire [31:0] n8_bit_left_shifter_1_out_3, shifter_1_out;

  and and_1 (and_1_out, not_1_out, in_2[0]);
  not not_1 (not_1_out, in_2[1]);
  not not_2 (not_2_out, in_2[0]);
  assign bit_extender_1_out = {{4{1'b0}}, and_1_out};  // Bit_Extender_part bit_extender_1
  and and_2 (and_2_out, in_2[1], not_2_out);
  Shifter_part #(.width(32), .shift("ar")) shifter_1 (.in(in_1), .\dist (bit_extender_1_out), .out(shifter_1_out));
  _8_bit_Left_Shifter u_8_bit_left_shifter_1 (.in_1(in_1), .in_2(and_2_out), .out_3(n8_bit_left_shifter_1_out_3));
  assign OUTPUT = and_3_out ? in_1 : 32'bz;  // Controlled_Buffer controlled_buffer_1
  and and_3 (and_3_out, not_1_out, not_2_out);
  assign OUTPUT = and_1_out ? shifter_1_out : 32'bz;  // Controlled_Buffer controlled_buffer_2
  assign OUTPUT = and_2_out ? n8_bit_left_shifter_1_out_3 : 32'bz;  // Controlled_Buffer controlled_buffer_3
endmodule

module _8_bit_Left_Shifter (
  input  [31:0] in_1,
  input  in_2,
  output [31:0] out_3
);

  wire [4:0] bit_extender_1_out;
  wire [31:0] shifter_1_out, shifter_2_out, shifter_3_out, shifter_4_out, shifter_5_out, shifter_6_out,
       shifter_7_out;

  assign bit_extender_1_out = {{4{1'b0}}, in_2};  // Bit_Extender_part bit_extender_1
  Shifter_part #(.width(32)) shifter_1 (.in(in_1), .\dist (bit_extender_1_out), .out(shifter_1_out));
  Shifter_part #(.width(32)) shifter_2 (.in(shifter_1_out), .\dist (bit_extender_1_out), .out(shifter_2_out));
  Shifter_part #(.width(32)) shifter_3 (.in(shifter_2_out), .\dist (bit_extender_1_out), .out(shifter_3_out));
  Shifter_part #(.width(32)) shifter_4 (.in(shifter_3_out), .\dist (bit_extender_1_out), .out(shifter_4_out));
  Shifter_part #(.width(32)) shifter_5 (.in(shifter_4_out), .\dist (bit_extender_1_out), .out(shifter_5_out));
  Shifter_part #(.width(32)) shifter_6 (.in(shifter_5_out), .\dist (bit_extender_1_out), .out(shifter_6_out));
  Shifter_part #(.width(32)) shifter_7 (.in(shifter_6_out), .\dist (bit_extender_1_out), .out(shifter_7_out));
  Shifter_part #(.width(32)) shifter_8 (.in(shifter_7_out), .\dist (bit_extender_1_out), .out(out_3));
endmodule

module Microarchitecture_Level (
  input  in_1,
  input  in_2,
  input  GLOBAL_RESET,
  output [31:0] Shifter_to_Registers,
  output [31:0] MAR_to_RAM,
  output [31:0] MDR_to_RAM,
  output [31:0] RAM_to_MDR,
  output [23:0] PC_to_RAM,
  output [7:0] RAM_to_MBR,
  output [8:0] MPC_to_Control_Store,
  output [8:0] Control_Store_to_Address,
  output [2:0] Control_Store_to_JAM,
  output [7:0] Control_Store_to_ALU,
  output [8:0] Control_Store_to_C_bus,
  output [2:0] Control_Store_to_MEM,
  output [3:0] Control_Store_to_B_bus,
  output [7:0] MBR_to_O,
  output [8:0] Address_to_O,
  output [1:0] JAM_to_High_Bit,
  output [1:0] ALU_to_Shifter_Control,
  output [5:0] ALU_to_ALU_Control,
  output [2:0] Memory_to_Registers,
  output [3:0] B_bus_to_Decoder
);

  wire b, clock_1_out, d_ff_1_q, d_ff_2_q, high_bit_1_output, main_1_n, main_1_z, mar_1_out_6, mdr_1_out_7,
       mir_first_20_bits_1_jmpc, mir_last_16_bits_1_cpp, mir_last_16_bits_1_h, mir_last_16_bits_1_lv,
       mir_last_16_bits_1_mar, mir_last_16_bits_1_mdr, mir_last_16_bits_1_opc, mir_last_16_bits_1_pc,
       mir_last_16_bits_1_sp, mir_last_16_bits_1_tos, n4_16_decoder_1_cpp, n4_16_decoder_1_lv,
       n4_16_decoder_1_mbr, n4_16_decoder_1_mbr_2, n4_16_decoder_1_mdr, n4_16_decoder_1_opc,
       n4_16_decoder_1_pc, n4_16_decoder_1_sp, n4_16_decoder_1_tos, not_1_out, w, x, z;
  wire [7:0] controlled_buffer_3_out, pc_1_out_7;
  wire [23:0] controlled_buffer_1_out;
  wire [31:0] CPP_q, H_q, LV_q, main_1_output, mbr_1_out_6, mdr_1_out_9, OPC_q, pc_1_out_8, SP_q, StoReg,
       TOS_q;

  assign controlled_buffer_1_out = mdr_1_out_7 ? MDR_to_RAM[23:0] : 24'bz;  // Controlled_Buffer controlled_buffer_1
  assign controlled_buffer_1_out = b ? PC_to_RAM : 24'bz;  // Controlled_Buffer controlled_buffer_2
  Bit_Extender bit_extender_1 (.in_1(pc_1_out_7), .out_2(PC_to_RAM));
  assign {controlled_buffer_3_out, controlled_buffer_1_out} = mar_1_out_6 ? MAR_to_RAM : 32'bz;  // Controlled_Buffer controlled_buffer_3
  not not_1 (not_1_out, b);
  RAM ram_1 (
    .Type(not_1_out), .MBR(RAM_to_MBR), .Addr(controlled_buffer_1_out), .in_6(z), .mcs(Memory_to_Registers),
    .MDR(RAM_to_MDR), .in_2(z), .in_1(GLOBAL_RESET));
  MAR mar_1 (
    .in_1(Memory_to_Registers), .in_2(StoReg), .out_7(MAR_to_RAM), .in_3(GLOBAL_RESET),
    .in_4(mir_last_16_bits_1_mar), .in_5(x), .out_6(mar_1_out_6));
  Register #(.width(32), .trigger("falling")) SP (
    .D(StoReg), .en(mir_last_16_bits_1_sp), .Q(SP_q), .clk(x), .clr(GLOBAL_RESET));
  Register #(.width(32), .trigger("falling")) LV (
    .D(StoReg), .en(mir_last_16_bits_1_lv), .Q(LV_q), .clk(x), .clr(GLOBAL_RESET));
  Register #(.width(32), .trigger("falling")) CPP (
    .D(StoReg), .en(mir_last_16_bits_1_cpp), .Q(CPP_q), .clk(x), .clr(GLOBAL_RESET));
  Register #(.width(32), .trigger("falling")) TOS (
    .D(StoReg), .en(mir_last_16_bits_1_tos), .Q(TOS_q), .clk(x), .clr(GLOBAL_RESET));
  Register #(.width(32), .trigger("falling")) OPC (
    .D(StoReg), .en(mir_last_16_bits_1_opc), .Q(OPC_q), .clk(x), .clr(GLOBAL_RESET));
  Register #(.width(32), .trigger("falling")) H (
    .D(StoReg), .en(mir_last_16_bits_1_h), .Q(H_q), .clk(x), .clr(GLOBAL_RESET));
  MDR mdr_1 (
    .in_1(Memory_to_Registers), .in_2(RAM_to_MDR), .in_3(StoReg), .out_8(MDR_to_RAM), .out_9(mdr_1_out_9),
    .in_4(GLOBAL_RESET), .in_5(mir_last_16_bits_1_mdr), .in_6(x), .out_7(mdr_1_out_7));
  PC pc_1 (
    .in_2(StoReg), .out_7(pc_1_out_7), .out_8(pc_1_out_8), .in_3(GLOBAL_RESET), .in_4(mir_last_16_bits_1_pc),
    .in_5(x), .in_1(Memory_to_Registers), .out_6(b));
  MBR mbr_1 (
    .in_1(RAM_to_MBR), .in_2(x), .Signed(n4_16_decoder_1_mbr_2), .Unsigned(n4_16_decoder_1_mbr),
    .out_6(mbr_1_out_6), .out_7(mbr_1_out_6), .out_5(MBR_to_O));
  assign mbr_1_out_6 = n4_16_decoder_1_sp ? SP_q : 32'bz;  // Controlled_Buffer controlled_buffer_4
  assign mbr_1_out_6 = n4_16_decoder_1_lv ? LV_q : 32'bz;  // Controlled_Buffer controlled_buffer_5
  assign mbr_1_out_6 = n4_16_decoder_1_cpp ? CPP_q : 32'bz;  // Controlled_Buffer controlled_buffer_6
  assign mbr_1_out_6 = n4_16_decoder_1_tos ? TOS_q : 32'bz;  // Controlled_Buffer controlled_buffer_7
  assign mbr_1_out_6 = n4_16_decoder_1_opc ? OPC_q : 32'bz;  // Controlled_Buffer controlled_buffer_8
  assign mbr_1_out_6 = n4_16_decoder_1_mdr ? mdr_1_out_9 : 32'bz;  // Controlled_Buffer controlled_buffer_9
  assign mbr_1_out_6 = n4_16_decoder_1_pc ? pc_1_out_8 : 32'bz;  // Controlled_Buffer controlled_buffer_10
  main main_1 (.OUTPUT(main_1_output), .A(H_q), .B(mbr_1_out_6), .N(main_1_n), .Z(main_1_z), .in_3(ALU_to_ALU_Control));
  Shifter shifter_1 (.in_1(main_1_output), .OUTPUT(StoReg), .in_2(ALU_to_Shifter_Control));
  // Probe on RAM_to_MBR
  D_Flip_Flop d_ff_1 (.clk(x), .D(main_1_n), .Q(d_ff_1_q), .en(1'b1), .reset(GLOBAL_RESET));  // open: Qn, preset
  _4_16_Decoder u_4_16_decoder_1 (
    .B_bus(B_bus_to_Decoder), .MDR(n4_16_decoder_1_mdr), .PC(n4_16_decoder_1_pc), .MBR(n4_16_decoder_1_mbr),
    .MBR_2(n4_16_decoder_1_mbr_2), .SP(n4_16_decoder_1_sp), .LV(n4_16_decoder_1_lv),
    .CPP(n4_16_decoder_1_cpp), .TOS(n4_16_decoder_1_tos), .OPC(n4_16_decoder_1_opc));
  O o_1 (
    .JMPC(mir_first_20_bits_1_jmpc), .MBR(MBR_to_O), .Address(Address_to_O), .Output(MPC_to_Control_Store),
    .in_4(high_bit_1_output));
  High_bit high_bit_1 (.Output(high_bit_1_output), .N(d_ff_1_q), .Z(d_ff_2_q), .J(JAM_to_High_Bit));
  D_Flip_Flop d_ff_2 (.clk(x), .D(main_1_z), .Q(d_ff_2_q), .en(1'b1), .reset(GLOBAL_RESET));  // open: Qn, preset
  MIR___First_20_bits mir_first_20_bits_1 (
    .Next_Address(Control_Store_to_Address), .JAM(Control_Store_to_JAM), .ALU(Control_Store_to_ALU),
    .Next_Address_2(Address_to_O), .JMPC(mir_first_20_bits_1_jmpc), .JAMN_JAMZ(JAM_to_High_Bit),
    .Shifter_Control(ALU_to_Shifter_Control), .ALU_Control(ALU_to_ALU_Control), .Reset(GLOBAL_RESET),
    .NA_Clock(w), .ALU_Clock(w), .in_5(w));
  Clock_part clock_1 (.out(clock_1_out));
  Control_Store control_store_1 (
    .in_1(MPC_to_Control_Store), .Address(Control_Store_to_Address), .J(Control_Store_to_JAM),
    .ALU(Control_Store_to_ALU), .C_bus(Control_Store_to_C_bus), .MEM(Control_Store_to_MEM),
    .B_bus(Control_Store_to_B_bus));
  MIR___Last_16_bits mir_last_16_bits_1 (
    .C_bus(Control_Store_to_C_bus), .Mem(Control_Store_to_MEM), .B_Bus(Control_Store_to_B_bus),
    .H(mir_last_16_bits_1_h), .OPC(mir_last_16_bits_1_opc), .TOS(mir_last_16_bits_1_tos),
    .CPP(mir_last_16_bits_1_cpp), .LV(mir_last_16_bits_1_lv), .SP(mir_last_16_bits_1_sp),
    .PC(mir_last_16_bits_1_pc), .MDR(mir_last_16_bits_1_mdr), .MAR(mir_last_16_bits_1_mar),
    .Memory_Control_Signals(Memory_to_Registers), .Decoder(B_bus_to_Decoder), .in_4(w), .in_3(GLOBAL_RESET));
  // Clock clock_2: pin names not known; wires that end beside it: clock_1_out, in_1, in_2, w, x, z
  // Probe on Shifter_to_Registers
  // Probe on MAR_to_RAM
  // Probe on MDR_to_RAM
  // Probe on RAM_to_MDR
  // Probe on PC_to_RAM
  // Probe on RAM_to_MBR
  // Probe on MPC_to_Control_Store
  // Probe on Control_Store_to_Address
  // Probe on Control_Store_to_JAM
  // Probe on Control_Store_to_ALU
  // Probe on Control_Store_to_C_bus
  // Probe on Control_Store_to_MEM
  // Probe on Control_Store_to_B_bus
  // Probe on MBR_to_O
  // Probe on Address_to_O
  // Probe on JAM_to_High_Bit
  // Probe on ALU_to_Shifter_Control
  // Probe on ALU_to_ALU_Control
  // Probe on Memory_to_Registers
  // Probe on B_bus_to_Decoder

  // Other names for the same wires on the sheet: ADDR2O[8:0] = Address_to_O; ALU2ALUC[5:0] = ALU_to_ALU_Control;
  //   ALU2SC[1:0] = ALU_to_Shifter_Control; BB2DEC[3:0] = B_bus_to_Decoder; CLR = GLOBAL_RESET;
  //   CS2ADDR[8:0] = Control_Store_to_Address; CS2ALU[7:0] = Control_Store_to_ALU;
  //   CS2BB[3:0] = Control_Store_to_B_bus; CS2CB[8:0] = Control_Store_to_C_bus; CS2JAM[2:0] = Control_Store_to_JAM;
  //   CS2MEM[2:0] = Control_Store_to_MEM; JAM2HB[1:0] = JAM_to_High_Bit; MAR2R[31:0] = MAR_to_RAM;
  //   MBR2O[7:0] = MBR_to_O; mcs[2:0] = Memory_to_Registers; MPC2CS[8:0] = MPC_to_Control_Store;
  //   PC2R[23:0] = PC_to_RAM; R2MBR[7:0] = RAM_to_MBR; R2MDR[31:0] = RAM_to_MDR; rout[31:0] = MDR_to_RAM;
  //   S2Reg[31:0] = Shifter_to_Registers

  // Notes on the sheet:
  //   MASTER CLOCK
  //   O
  //   MIR
  //   OUTPUTS
  //   Registers
  //   Control Store
  //   |
endmodule

module High_bit (
  input  [1:0] J,
  input  N,
  input  Z,
  output Output
);

  wire and_1_out, and_2_out;

  or or_1 (Output, and_1_out, and_2_out);
  and and_1 (and_1_out, N, J[1]);
  and and_2 (and_2_out, Z, J[0]);

  // Notes on the sheet:
  //   JAMN
  //   JAMZ
endmodule

module MIR___First_20_bits (
  input  [8:0] Next_Address,
  input  NA_Clock,
  input  [2:0] JAM,
  input  Reset,
  input  in_5,
  input  [7:0] ALU,
  input  ALU_Clock,
  output [8:0] Next_Address_2,
  output JMPC,
  output [1:0] JAMN_JAMZ,
  output [1:0] Shifter_Control,
  output [5:0] ALU_Control
);

  Register #(.width(9)) register_1 (.D(Next_Address), .en(1'b1), .Q(Next_Address_2), .clk(NA_Clock), .clr(Reset));
  Register #(.width(3)) register_2 (.D(JAM), .en(1'b1), .Q({JMPC, JAMN_JAMZ}), .clk(in_5), .clr(Reset));
  Register register_3 (.D(ALU), .en(1'b1), .Q({Shifter_Control, ALU_Control}), .clk(ALU_Clock), .clr(Reset));
endmodule

module MIR___Last_16_bits (
  input  [8:0] C_bus,
  input  [2:0] Mem,
  input  in_3,
  input  in_4,
  input  [3:0] B_Bus,
  output H,
  output OPC,
  output TOS,
  output CPP,
  output LV,
  output SP,
  output PC,
  output MDR,
  output MAR,
  output [2:0] Memory_Control_Signals,
  output [3:0] Decoder
);

  Register #(.width(9)) register_1 (
    .D(C_bus), .en(1'b1), .Q({H, OPC, TOS, CPP, LV, SP, PC, MDR, MAR}), .clk(in_4), .clr(in_3));
  Register #(.width(3)) register_2 (.D(Mem), .en(1'b1), .Q(Memory_Control_Signals), .clk(in_4), .clr(in_3));
  Register #(.width(4)) register_3 (.D(B_Bus), .en(1'b1), .Q(Decoder), .clk(in_4), .clr(in_3));
endmodule

module MPC (
  input  [8:0] in_1,
  output [8:0] Going_into_Microprogam
);

  wire undriven;

  Register #(.width(9)) MPC (.D(in_1), .Q(Going_into_Microprogam), .clk(undriven));  // open: en, clr
endmodule

module _4_16_Decoder (
  input  [3:0] B_bus,
  output MDR,
  output PC,
  output MBR,
  output MBR_2,
  output SP,
  output LV,
  output CPP,
  output TOS,
  output OPC
);

  Decoder_part #(.select(4), .enable("false")) decoder_1 (
    .out0(MDR), .out1(PC), .out2(MBR), .out3(MBR_2), .out4(SP), .out5(LV), .out6(CPP), .out7(TOS),
    .out8(OPC), .sel(B_bus));  // open: out9, out10, out11, out12, out13, out14, out15
endmodule

module Control_Store (
  input  [8:0] in_1,
  output [8:0] Address,
  output [7:0] ALU,
  output [8:0] C_bus,
  output [3:0] B_bus,
  output [2:0] J,
  output [2:0] MEM
);

  // Probe on Address
  ROM #(.addrWidth(9), .dataWidth(20)) rom_1 (.addr(in_1), .data({Address, J, ALU}));  // open: sel
  ROM #(.addrWidth(9), .dataWidth(16)) rom_2 (.addr(in_1), .data({C_bus, MEM, B_bus}));  // open: sel

  // Notes on the sheet:
  //   contents of rom_1 (hex, n*v repeats v):
  //   1000 11835 435 2014 103c 301c b83c 4014 4814 5014 5836 1018 100c 1014 7814 910 8835 9035 1000 a035
  //   2890 b014 b83c c035 c835 1014 1010 e01c e83d f014 f814 10035 10814 11015 1014 12035 1010 13090 13835
  //   1409c 14835 1509c 1581c 16035 1018 17090 17835 1809c 18835 1909c 1981c 1a035 1018 7f000 1b814 1c03c
  //   1c814 1d036 1d835 1014 7f000 1f090 1f835 2009c 20835 2109c 2181c 22035 1018 23090 23835 2409c 24835
  //   2509c 2581c 26018 1010 10*7f000 2c036 6810 2d035 1014 4*7f000 3834 1836 7f000 7f000 7f000 3283e
  //   33014 103f 14*7f000 22835 16835 12835 1e835 5*7f000 3f836 6014 40836 41014 101c 7f000 42814 4303c
  //   43835 44014 44835 103c 15*7f000 4d036 7014 4e036 4e814 4f014 a10 50036 50836 51014 51814 52014 93f
  //   7f000 7f000 54036 54835 55090 5581c d03c 56814 57010 57814 58035 58814 59014 59814 1014 7f000 7f000
  //   5b835 5c090 5c81c 5d03c 5d835 5e014 5e835 5f090 5f81c 60035 6083f 61035 61835 d890 62835 80410
  //   59*7f000 54036 19*7f000 8b035 8b890 8c01c b83c 29*7f000 9b835 9c090 9c81c 1c03c 6*7f000
  //   contents of rom_2 (hex, n*v repeats v):
  //   0 201 211 8007 2140 8003 a6 84 8040 107 c4 2000 2140 2000 2000 8 484 211 2142 211 8003 8005 a3 484
  //   251 2000 0 8003 144 480 148 484 145 211 807 211 0 8003 211 8003 211 8003 8003 211 400 8003 211 8003
  //   211 8003 8003 211 800 0 8005 a3 147 4a4 211 2000 0 8003 211 8003 211 8003 8003 211 1000 8003 211
  //   8003 211 8003 8003 200 11*0 4a4 0 484 147 4*0 a4 4a4 0 0 0 4a4 8007 2140 14*0 4*211 5*0 4a4 8007 4a4
  //   8007 2140 0 8005 a3 211 8000 211 142 15*0 4a4 4007 4a4 4007 2000 8 4a4 484 8020 4007 2000 8 0 0 4001
  //   211 8002 8003 218 4a5 0 8a0 85 230 84 800 147 0 0 210 8003 8003 a6 4001 210 211 8003 8003 211 2004
  //   2087 211 8003 211 60*0 4011 19*0 211 8003 8003 a5 29*0 211 8003 8003 85
endmodule

module MBR (
  input  [7:0] in_1,
  input  in_2,
  input  Signed,
  input  Unsigned,
  output [7:0] out_5,
  output [31:0] out_6,
  output [31:0] out_7
);

  wire [7:0] controlled_buffer_1_out, controlled_buffer_2_out;
  wire [31:0] bit_extender_1_out, bit_extender_2_out;

  Register #(.trigger("falling")) MBR (.D(in_1), .en(1'b1), .Q(out_5), .clk(in_2));  // open: clr
  assign controlled_buffer_1_out = Signed ? out_5 : 8'bz;  // Controlled_Buffer controlled_buffer_1
  assign controlled_buffer_2_out = Unsigned ? out_5 : 8'bz;  // Controlled_Buffer controlled_buffer_2
  assign bit_extender_1_out = {{24{controlled_buffer_1_out[7]}}, controlled_buffer_1_out};  // Bit_Extender_part bit_extender_1
  assign bit_extender_2_out = {{24{1'b0}}, controlled_buffer_2_out};  // Bit_Extender_part bit_extender_2
  assign out_6 = Signed ? bit_extender_1_out : 32'bz;  // Controlled_Buffer controlled_buffer_3
  assign out_7 = Unsigned ? bit_extender_2_out : 32'bz;  // Controlled_Buffer controlled_buffer_4
endmodule

module O (
  input  JMPC,
  input  [7:0] MBR,
  input  [8:0] Address,
  input  in_4,
  output [8:0] Output
);

  wire not_1_out;
  wire [7:0] or_2_out;

  or or_1 (Output[8], Address[8], in_4);
  assign or_2_out = MBR | Address[7:0];  // OR_Gate or_2, 8 bits wide
  not not_1 (not_1_out, JMPC);
  assign Output[7:0] = JMPC ? or_2_out : 8'bz;  // Controlled_Buffer controlled_buffer_1
  assign Output[7:0] = not_1_out ? Address[7:0] : 8'bz;  // Controlled_Buffer controlled_buffer_2
endmodule

module MAR (
  input  [2:0] in_1,
  input  [31:0] in_2,
  input  in_3,
  input  in_4,
  input  in_5,
  output out_6,
  output [31:0] out_7
);

  wire [31:0] MAR_q;

  Register #(.width(32), .trigger("falling")) MAR (.D(in_2), .en(in_4), .Q(MAR_q), .clk(in_5), .clr(in_3));
  assign out_7 = in_1[2] ? MAR_q : 32'bz;  // Controlled_Buffer controlled_buffer_1

  assign out_6 = in_1[2];
endmodule

module PC (
  input  [2:0] in_1,
  input  [31:0] in_2,
  input  in_3,
  input  in_4,
  input  in_5,
  output out_6,
  output [7:0] out_7,
  output [31:0] out_8
);

  wire [31:8] controlled_buffer_1_out;

  Register #(.width(32), .trigger("falling")) PC (.D(in_2), .en(in_4), .Q(out_8), .clk(in_5), .clr(in_3));
  assign {controlled_buffer_1_out, out_7} = in_1[0] ? out_8 : 32'bz;  // Controlled_Buffer controlled_buffer_1

  assign out_6 = in_1[0];
endmodule

module MDR (
  input  [2:0] in_1,
  input  [31:0] in_2,
  input  [31:0] in_3,
  input  in_4,
  input  in_5,
  input  in_6,
  output out_7,
  output [31:0] out_8,
  output [31:0] out_9
);

  wire not_1_out, not_2_out;
  wire [31:0] controlled_buffer_1_out, MDR_q;

  assign controlled_buffer_1_out = in_1[1] ? in_2 : 32'bz;  // Controlled_Buffer controlled_buffer_1
  not not_1 (not_1_out, in_1[1]);
  assign controlled_buffer_1_out = not_1_out ? in_3 : 32'bz;  // Controlled_Buffer controlled_buffer_2
  Register #(.width(32), .trigger("falling")) MDR (
    .D(controlled_buffer_1_out), .en(in_5), .Q(MDR_q), .clk(in_6), .clr(in_4));
  assign out_8 = in_1[2] ? MDR_q : 32'bz;  // Controlled_Buffer controlled_buffer_3
  not not_2 (not_2_out, in_1[2]);
  assign out_9 = not_2_out ? MDR_q : 32'bz;  // Controlled_Buffer controlled_buffer_4

  assign out_7 = in_1[2];

  // Notes on the sheet:
  //   RAM
  //   C-Bus
  //   Reading
  //   Writing
  //   RAM IN
  //   B-Bus
endmodule

module RAM (
  input  in_1,
  input  in_2,
  input  [23:0] Addr,
  input  Type,
  input  [2:0] mcs,
  input  in_6,
  output [31:0] MDR,
  output [7:0] MBR
);

  wire not_1_out;
  wire [7:0] multiplexer_1_out;
  wire [23:0] controlled_buffer_1_out;
  wire [31:0] ram_1_data;

  not not_1 (not_1_out, Type);
  assign controlled_buffer_1_out = Type ? Addr : 24'bz;  // Controlled_Buffer controlled_buffer_1
  assign controlled_buffer_1_out = not_1_out ? {2'b00, Addr[23:2]} : 24'bz;  // Controlled_Buffer controlled_buffer_2
  // Probe on controlled_buffer_1_out
  // Probe on Addr[1:0]
  RAM_part #(.addrWidth(24), .dataWidth(32)) ram_1 (
    .addr(controlled_buffer_1_out), .data(ram_1_data), .clk(in_6), .ld(1'b1));  // open: sel, clr
  Multiplexer #(.select(2), .width(8)) multiplexer_1 (
    .in0(ram_1_data[31:24]), .in1(ram_1_data[23:16]), .in2(ram_1_data[15:8]), .in3(ram_1_data[7:0]),
    .out(multiplexer_1_out), .sel(Addr[1:0]));  // open: en
  // Probe on ram_1_data[31:24]
  // Probe on ram_1_data[23:16]
  // Probe on ram_1_data[15:8]
  // Probe on ram_1_data[7:0]
  // Probe on multiplexer_1_out
  Cache cache_1 (
    .MDR(ram_1_data), .MBR(multiplexer_1_out), .MDR_2(MDR), .MBR_2(MBR), .Writing(mcs[2]), .Fetching(mcs[0]),
    .in_6(in_2), .in_4(in_1));
  // Probe on MBR

  // Notes on the sheet:
  //   Using word addressable memory
  //   if type = 0 then Addr is a byte address
  //   if type = 1 then Addr is a word address
  //   Goal: if given a byte address, load MBR a byte out of memory
  //   Set the type = 0 and place the byte address in Addr
  //   Goal: if given a word address, load MDR with 4 bytes out of memory
  //    Set the type=1 and place the word address into Addr
  //   How to read a byte or word from memory when given a byte or word addres.  A word is defined to be 32 bits.
  //   to select one byte out of the 32-bits.
  //   Note the byte address is shifted into a word address.  The word address is
  //   fed into the RAM module.  The output from the RAM module is split into four bytes.
  //   The lower two bits of the original byte address is fed into the multiplexer
endmodule

module Bit_Extender (
  input  [7:0] in_1,
  output [23:0] out_2
);

  assign out_2 = {{16{1'b0}}, in_1};  // Bit_Extender_part bit_extender_1
endmodule

module Cache (
  input  [31:0] MDR,
  input  Writing,
  input  [7:0] MBR,
  input  in_4,
  input  Fetching,
  input  in_6,
  output [31:0] MDR_2,
  output [7:0] MBR_2
);

  wire [7:0] MBR_q;
  wire [31:0] MDR_q;

  Register #(.width(32), .trigger("falling")) u_MDR (.D(MDR), .en(1'b1), .Q(MDR_q), .clk(in_6), .clr(in_4));
  assign MDR_2 = Writing ? MDR_q : 32'bz;  // Controlled_Buffer controlled_buffer_1
  Register #(.trigger("falling")) u_MBR (.D(MBR), .en(1'b1), .Q(MBR_q), .clk(in_6), .clr(in_4));
  assign MBR_2 = Fetching ? MBR_q : 8'bz;  // Controlled_Buffer controlled_buffer_2
endmodule

module Clock (
  input  in_1,
  input  in_2,
  output out_3,
  output out_4,
  output out_5,
  output out_6
);

  wire j_k_ff_1_q, j_k_ff_2_q, j_k_ff_2_qn, j_k_ff_3_q, j_k_ff_3_qn;

  J_K_Flip_Flop #(.trigger("falling")) j_k_ff_1 (
    .J(1'b1), .clk(in_1), .K(1'b1), .Q(j_k_ff_1_q), .reset(in_2));  // open: Qn, preset, en
  J_K_Flip_Flop #(.trigger("falling")) j_k_ff_2 (
    .J(1'b1), .clk(j_k_ff_1_q), .K(1'b1), .Q(j_k_ff_2_q), .Qn(j_k_ff_2_qn), .reset(in_2));  // open: preset, en
  J_K_Flip_Flop #(.trigger("falling")) j_k_ff_3 (
    .J(1'b1), .clk(j_k_ff_2_q), .K(1'b1), .Q(j_k_ff_3_q), .Qn(j_k_ff_3_qn), .reset(in_2));  // open: preset, en
  and and_1 (out_3, j_k_ff_1_q, j_k_ff_2_q, j_k_ff_3_q);
  and and_2 (out_4, j_k_ff_1_q, j_k_ff_2_qn, j_k_ff_3_q);
  and and_3 (out_5, j_k_ff_3_qn, j_k_ff_2_q, j_k_ff_1_q);
  and and_4 (out_6, j_k_ff_3_qn, j_k_ff_2_qn, j_k_ff_1_q);
endmodule
